# Fritzing sketch breadboard (saved by Fritzing 0.9.2b)
breadboards: 1

parts:
  U2 = attiny85 [package=dip]
  U4 = POT [package=pot_mammoth]
  7805 = Voltage Regulator [package=to-220-alt]
  VCC1 = Battery block 9V
  SPKR1 = Loudspeaker

nets:
  N1: U2.Pin_3, U4.A
  N2: U2.Pin_5, SPKR1.pin2
  N3: U2.Pin_8, U4.S, 7805.OUT
  N4: U4.E, 7805.GND, VCC1.-, SPKR1.pin1
  N5: 7805.IN, VCC1.+
